# Fritzing sketch RPI_Wiring (saved by Fritzing 0.9.3b)

parts:
  MCU1 = Raspberry Pi Zero
  J1 = Basic Servo

nets:
  N1: MCU1.pin_2, MCU1.pin_4, J1.vcc
  N2: MCU1.pin_7, J1.pulse
  N3: MCU1.pin_9, MCU1.pin_39, J1.gnd
